// Digital circuit 32bit-register.dig as structural Verilog
module _32bit_register (
  input  [31:0] Data,
  input  EN,
  input  CLR,
  input  CLK,
  output [31:0] Q
);

  wire or_1_out;
  wire [31:0] multiplexer_1_out;

  Multiplexer #(.Bits(32)) multiplexer_1 (.sel(CLR), .in_0(Data), .in_1({32{1'b0}}), .out(multiplexer_1_out));
  or or_1 (or_1_out, EN, CLR);
  Register #(.Bits(32)) register_1 (.D(multiplexer_1_out), .C(CLK), .en(or_1_out), .Q(Q));
endmodule
