// Digital circuit Extender.dig as structural Verilog
module Extender (
  input  [31:0] IW,
  input  [1:0] EXTOP,
  output [31:0] extimm
);

  wire [31:0] bitextender_1_out;
  wire [63:0] mul_1_mul;

  BitExtender #(.inputBits(24), .outputBits(32)) bitextender_1 (.in(IW[23:0]), .out(bitextender_1_out));
  Mul #(.Bits(32)) mul_1 (.a(bitextender_1_out), .b(32'h4), .mul(mul_1_mul));
  Multiplexer #(.Selector_Bits(2), .Bits(32)) multiplexer_1 (
    .sel(EXTOP), .in_0({{24{1'b0}}, IW[7:0]}), .in_1({{20{1'b0}}, IW[11:0]}), .in_2(mul_1_mul[31:0]),
    .in_3({{27{1'b0}}, IW[11:7]}), .out(extimm));

  // Notes on the sheet:
  //   DP Case
  //   Memory Case
  //   Branch Case
  //   Move Case
endmodule
