// Digital circuit Instruction Memory.dig as structural Verilog
module Instruction_Memory (
  input  [6:0] PC,
  input  [2:0] sel,
  output [31:0] iw
);

  wire [31:0] fact_d, quadratic_d, search_d, sort_d, sum_array_d;

  ROM #(.AddrBits(7), .Bits(32)) quadratic (.A(PC), .sel(1'b1), .D(quadratic_d));
  ROM #(.AddrBits(7), .Bits(32)) fact (.A(PC), .sel(1'b1), .D(fact_d));
  ROM #(.AddrBits(7), .Bits(32)) sum_array (.A(PC), .sel(1'b1), .D(sum_array_d));
  ROM #(.AddrBits(7), .Bits(32)) search (.A(PC), .sel(1'b1), .D(search_d));
  ROM #(.AddrBits(7), .Bits(32)) sort (.A(PC), .sel(1'b1), .D(sort_d));
  Multiplexer #(.Selector_Bits(3), .Bits(32)) multiplexer_1 (
    .sel(sel), .in_0(quadratic_d), .in_1(fact_d), .in_2(sum_array_d), .in_3(search_d), .in_4(sort_d),
    .in_5({32{1'b0}}), .in_6({32{1'b0}}), .in_7({32{1'b0}}), .out(iw));

  // Notes on the sheet:
  //   contents of quadratic (hex, n*v repeats v):
  //   e3a00002,e3a01004,e3a02008,e3a03010,eb000000,e2800000,e0020092,e0822003,e0000090,
  //   e0000190,e0800002,e12fff1e
  //   contents of fact (hex, n*v repeats v):
  //   e3a00005,e28dd028,eb000000,e2800000,e24dd008,e58de000,e58d1004,e3500001,a000003,e1a01000,
  //   e2400001,ebfffff7,e0000190,e59d1004,e59de000,e28dd008,e12fff1e
  //   contents of sum_array (hex, n*v repeats v):
  //   e3a0d080,e24dd018,e3a00000,e58d0000,e3a00004,e58d0004,e3a00008,e58d0008,e3a0000c,
  //   e58d000c,e3a00010,e58d0010,e1a0000d,e3a01005,eb000000,e2800000,e3a02000,e3a03000,
  //   e1520001,a000004,e590c000,e083300c,e2822001,e2800004,eafffff8,e1a00003,e12fff1e
  //   contents of search (hex, n*v repeats v):
  //   e3a0d080,e24dd018,e3a00000,e58d0000,e3a00004,e58d0004,e3a00008,e58d0008,e3a0000c,
  //   e58d000c,e3a00010,e58d0010,e1a0000d,e3a01000,e3a02004,e3a0300c,eb000000,e2800000,
  //   e1510002,ca000014,e0424001,e1a040a4,e0844001,e3a0c004,e00c0c94,e790c00c,e153000c,
  //   a00000d,ba000000,ea000001,e2442001,ea000001,e2841001,eaffffff,e24dd008,e58de000,ebffffec,
  //   e59de000,e28dd008,e1a04000,ea000000,ffffffff,e1a00004,e12fff1e
  //   contents of sort (hex, n*v repeats v):
  //   e3a0d080,e24dd018,e3a00010,e58d0000,e3a00004,e58d0004,e3a00020,e58d0008,e3a00002,
  //   e58d000c,e3a00008,e58d0010,e1a0000d,e3a01005,eb000005,e59d0000,e59d1004,e59d2008,
  //   e59d300c,e59d4010,e2800000,e24dd010,e58d0008,e1a03001,e3a02000,ea000010,e3a0c001,
  //   e3a01000,e5908000,e2800004,e153000c,1a000000,e12fff1e,e5909000,e2800004,e1580009,
  //   ba000000,ea000002,e1a0100c,e1a08009,eaffffff,e28cc001,eafffff2,e1520003,a000013,e58de004,
  //   e58d300c,e0433002,ebffffe8,e59d300c,e59de004,e1510002,1a000003,e2822001,e2800004,
  //   e58d0008,eafffff1,e3a00004,e0010190,e59d0008,e5906000,e7904001,e5804000,e7806001,
  //   eafffff3,e1a00003,e28dd010,e12fff1e
endmodule
