// Digital circuit Processor.dig as structural Verilog
module Processor (
  input  CLK,
  input  [2:0] Program_Selector,
  input  ON
);

  wire ALUsrcB, and_1_out, C, CLK_t, CLR, done, MR, MW, N, not_1_out, RFW, RR0sel, RR1sel, V, WDsel, WRsel, Z;
  wire [1:0] EXTop, PCsel;
  wire [2:0] ALUop;
  wire [3:0] multiplexer_2_out, multiplexer_3_out, multiplexer_4_out, NZCV, reg_input_decoder_1_readreg0,
       reg_input_decoder_1_readreg1, reg_input_decoder_1_writereg;
  wire [31:0] add_1_s, add_2_s, alu_1_r, extender_1_extimm, iw, multiplexer_1_out, multiplexer_5_out,
       multiplexer_6_out, multiplexer_7_out, PC_q, r0, r1, r2, r3, r4, r5, r6, r7, r8, r9, r10, r11, r12,
       r13, r14, r15, ramdualport_1_d, register_file_1_rd0, register_file_1_rd1;

  and and_1 (and_1_out, ON, CLK);
  DipSwitch u_CLR (.out(CLR));
  and and_2 (CLK_t, and_1_out, ~done);  // And
  _32bit_register PC (.Data(multiplexer_1_out), .EN(1'b1), .CLR(CLR), .CLK(CLK_t), .Q(PC_q));
  Multiplexer #(.Selector_Bits(2), .Bits(32)) multiplexer_1 (
    .sel(PCsel), .in_0(add_1_s), .in_1(multiplexer_7_out), .in_2(register_file_1_rd1), .in_3({32{1'b0}}),
    .out(multiplexer_1_out));
  decoder_main decoder_main_1 (
    .CLK(CLK_t), .NZCV(NZCV), .iw(iw), .RFW(RFW), .EXTop(EXTop), .ALUsrcB(ALUsrcB), .ALUop(ALUop),
    .PCsel(PCsel), .RR0sel(RR0sel), .RR1sel(RR1sel), .WRsel(WRsel), .WDsel(WDsel), .MR(MR), .MW(MW));
  Instruction_Memory instruction_memory_1 (.PC(PC_q[8:2]), .sel(Program_Selector), .iw(iw));
  Add #(.Bits(32)) add_1 (.a(PC_q), .b(32'h4), .c_i(1'b0), .s(add_1_s));  // open: c_o
  // Probe on iw
  // Probe on PCsel
  // Probe on EXTop
  reg_input_decoder reg_input_decoder_1 (
    .mul(RR1sel), .iw(iw), .readreg0(reg_input_decoder_1_readreg0), .writereg(reg_input_decoder_1_writereg),
    .readreg1(reg_input_decoder_1_readreg1));
  Add #(.Bits(32)) add_2 (.a(add_1_s), .b(32'h4), .c_i(1'b0), .s(add_2_s));  // open: c_o
  // Probe on r0
  // Probe on r1
  // Probe on r2
  // Probe on r3
  // Probe on r4
  // Probe on r5
  // Probe on r6
  // Probe on r7
  Multiplexer #(.Bits(4)) multiplexer_2 (
    .sel(RR0sel), .in_0(reg_input_decoder_1_readreg0), .in_1(4'b1111), .out(multiplexer_2_out));
  Multiplexer #(.Bits(4)) multiplexer_3 (
    .sel(MW), .in_0(reg_input_decoder_1_readreg1), .in_1(reg_input_decoder_1_writereg),
    .out(multiplexer_3_out));
  Multiplexer #(.Bits(4)) multiplexer_4 (
    .sel(WRsel), .in_0(reg_input_decoder_1_writereg), .in_1(4'b1110), .out(multiplexer_4_out));
  Multiplexer #(.Bits(32)) multiplexer_5 (
    .sel(WDsel), .in_0(multiplexer_7_out), .in_1(add_1_s), .out(multiplexer_5_out));
  // Probe on r8
  // Probe on r9
  // Probe on r10
  // Probe on r11
  register_file register_file_1 (
    .ReadReg0(multiplexer_2_out), .ReadReg1(multiplexer_3_out), .WriteData(multiplexer_5_out),
    .WriteReg(multiplexer_4_out), .WriteEnable(RFW), .CLR(CLR), .CLK(CLK_t), .PC(add_2_s),
    .Rd0(register_file_1_rd0), .Rd1(register_file_1_rd1), .r0(r0), .r1(r1), .r2(r2), .r3(r3), .r4(r4),
    .r5(r5), .r6(r6), .r7(r7), .r8(r8), .r9(r9), .r10(r10), .r11(r11), .r12(r12), .r13(r13), .r14(r14),
    .r15(r15));
  // Probe on r12
  // Probe on r13
  // Probe on r14
  // Probe on r15
  Multiplexer #(.Bits(32)) multiplexer_6 (
    .sel(ALUsrcB), .in_0(register_file_1_rd1), .in_1(extender_1_extimm), .out(multiplexer_6_out));
  Extender extender_1 (.IW(iw), .EXTOP(EXTop), .extimm(extender_1_extimm));
  ALU alu_1 (
    .A(register_file_1_rd0), .B(multiplexer_6_out), .ALUOP(ALUop), .R(alu_1_r), .NZCV(NZCV), .N(N), .Z(Z),
    .C(C), .V(V));
  Multiplexer #(.Bits(32)) multiplexer_7 (
    .sel(not_1_out), .in_0(ramdualport_1_d), .in_1(alu_1_r), .out(multiplexer_7_out));
  Comparator #(.Bits(32)) comparator_1 (.a(iw), .b(32'he2800000), .eq(done));  // open: gt, lt
  // Probe on extender_1_extimm
  not not_1 (not_1_out, MR);
  LED led_1 (.in(done));
  RAMDualPort #(.AddrBits(7), .Bits(32)) ramdualport_1 (
    .A(alu_1_r[8:2]), .Din(register_file_1_rd1), .str(MW), .C(CLK_t), .ld(MR), .D(ramdualport_1_d));

  // Other names for the same wires on the sheet: ProSel[2:0] = Program_Selector

  // Notes on the sheet:
  //   CLK: Hz: 2147483647
endmodule
