// Digital circuit decoder.dig as structural Verilog
module decoder (
  input  [3:0] SEL,
  input  EN,
  output r0,
  output r1,
  output r2,
  output r4,
  output r5,
  output r6,
  output r7,
  output r8,
  output r9,
  output r10,
  output r11,
  output r12,
  output r13,
  output r14,
  output r15,
  output r3
);

  wire decoder_1_out_0, decoder_1_out_1, decoder_1_out_2, decoder_1_out_3, decoder_1_out_4, decoder_1_out_5,
       decoder_1_out_6, decoder_1_out_7, decoder_1_out_8, decoder_1_out_9, decoder_1_out_10,
       decoder_1_out_11, decoder_1_out_12, decoder_1_out_13, decoder_1_out_14, decoder_1_out_15;

  Decoder #(.Selector_Bits(4)) decoder_1 (
    .sel(SEL), .out_0(decoder_1_out_0), .out_1(decoder_1_out_1), .out_2(decoder_1_out_2),
    .out_3(decoder_1_out_3), .out_4(decoder_1_out_4), .out_5(decoder_1_out_5), .out_6(decoder_1_out_6),
    .out_7(decoder_1_out_7), .out_8(decoder_1_out_8), .out_9(decoder_1_out_9), .out_10(decoder_1_out_10),
    .out_11(decoder_1_out_11), .out_12(decoder_1_out_12), .out_13(decoder_1_out_13),
    .out_14(decoder_1_out_14), .out_15(decoder_1_out_15));
  and and_1 (r0, decoder_1_out_0, EN);
  and and_2 (r1, decoder_1_out_1, EN);
  and and_3 (r2, decoder_1_out_2, EN);
  and and_4 (r3, decoder_1_out_3, EN);
  and and_5 (r4, decoder_1_out_4, EN);
  and and_6 (r5, decoder_1_out_5, EN);
  and and_7 (r6, decoder_1_out_6, EN);
  and and_8 (r7, decoder_1_out_7, EN);
  and and_9 (r8, decoder_1_out_8, EN);
  and and_10 (r9, decoder_1_out_9, EN);
  and and_11 (r10, decoder_1_out_10, EN);
  and and_12 (r11, decoder_1_out_11, EN);
  and and_13 (r12, decoder_1_out_12, EN);
  and and_14 (r13, decoder_1_out_13, EN);
  and and_15 (r14, decoder_1_out_14, EN);
  and and_16 (r15, decoder_1_out_15, EN);
endmodule
