// Digital circuit decoder_main.dig as structural Verilog
module decoder_main (
  input  CLK,
  input  [3:0] NZCV,
  input  [31:0] iw,
  output RFW,
  output [1:0] EXTop,
  output ALUsrcB,
  output [2:0] ALUop,
  output [1:0] PCsel,
  output RR0sel,
  output RR1sel,
  output WRsel,
  output WDsel,
  output MR,
  output MW
);

  wire AL_eq, and_1_out, and_2_out, and_3_out, and_4_out, and_5_out, and_6_out, C, condex, decoder_new_1_cmp,
       EQ_eq, GE_eq, GT_eq, LE_eq, LT_eq, N, NE_eq, NV, or_1_out, or_2_out, or_3_out, V, Z;
  wire [1:0] decoder_new_1_pcsel;

  Comparator comparator_1 (.a(N), .b(V), .eq(NV));  // open: gt, lt
  decoder_new decoder_new_1 (
    .IW(iw), .RFW(RFW), .EXTop(EXTop), .ALUsrcB(ALUsrcB), .ALUop(ALUop), .PCsel(decoder_new_1_pcsel),
    .RR0sel(RR0sel), .RR1sel(RR1sel), .WRsel(WRsel), .WDsel(WDsel), .CMP(decoder_new_1_cmp), .MR(MR), .MW(MW));
  Register #(.Bits(4)) register_1 (.D(NZCV), .C(CLK), .en(decoder_new_1_cmp), .Q({V, C, Z, N}));
  Comparator #(.Bits(4)) AL (.a(iw[31:28]), .b(4'b1110), .eq(AL_eq));  // open: gt, lt
  Comparator #(.Bits(4)) EQ (.a(iw[31:28]), .b(4'b0000), .eq(EQ_eq));  // open: gt, lt
  Comparator #(.Bits(4)) NE (.a(iw[31:28]), .b(4'b0001), .eq(NE_eq));  // open: gt, lt
  Comparator #(.Bits(4)) GE (.a(iw[31:28]), .b(4'b1010), .eq(GE_eq));  // open: gt, lt
  Comparator #(.Bits(4)) LT (.a(iw[31:28]), .b(4'b1011), .eq(LT_eq));  // open: gt, lt
  Comparator #(.Bits(4)) GT (.a(iw[31:28]), .b(4'b1100), .eq(GT_eq));  // open: gt, lt
  Comparator #(.Bits(4)) LE (.a(iw[31:28]), .b(4'b1101), .eq(LE_eq));  // open: gt, lt
  and and_1 (and_1_out, EQ_eq, Z);
  and and_2 (and_2_out, NE_eq, ~Z);  // And
  and and_3 (and_3_out, GE_eq, NV);
  and and_4 (and_4_out, LT_eq, ~NV);  // And
  and and_5 (and_5_out, GT_eq, ~Z, NV);  // And
  and and_6 (and_6_out, LE_eq, Z, ~NV);  // And
  Multiplexer #(.Bits(2)) multiplexer_1 (.sel(condex), .in_0(2'b00), .in_1(decoder_new_1_pcsel), .out(PCsel));
  or or_1 (or_1_out, AL_eq, and_1_out);
  or or_2 (or_2_out, and_2_out, and_3_out, and_4_out);
  or or_3 (or_3_out, and_5_out, and_6_out);
  or or_4 (condex, or_1_out, or_2_out, or_3_out);
endmodule
