// Digital circuit decoder_new.dig as structural Verilog
module decoder_new (
  input  [31:0] IW,
  output RFW,
  output [1:0] EXTop,
  output ALUsrcB,
  output [2:0] ALUop,
  output [1:0] PCsel,
  output RR0sel,
  output RR1sel,
  output WRsel,
  output WDsel,
  output CMP,
  output MR,
  output MW
);

  wire add_i_eq, add_r_eq, and_1_out, and_2_out, and_3_out, and_4_out, and_5_out, and_6_out, and_7_out,
       and_8_out, and_9_out, b_eq, bl_eq, bx_eq, cmp_i_eq, cmp_r_eq, comparator_1_eq, comparator_2_eq,
       ldr_i_eq, ldr_r_eq, lsl__i, lsl__r, lsr__i, lsr__r, mov_i_eq, mov_r_eq, mul_eq, str_i_eq, str_r_eq,
       sub_i_eq, sub_r_eq;
  wire [4:0] priorityencoder_1_num;
  wire [6:0] multiplexer_1_out;

  Comparator #(.Bits(12)) comparator_1 (.a(IW[27:16]), .b(12'h1a0), .eq(comparator_1_eq));  // open: gt, lt
  // Probe on IW[27:20]
  // Probe on IW[27:24]
  // Probe on IW[27:4]
  // Probe on IW[27:16]
  // Probe on IW[7:4]
  // Probe on IW[6:4]
  // Probe on IW[27:25]
  // Probe on IW[20]
  // Probe on IW[31:28]
  Comparator #(.Bits(4)) lsl_r (.a(IW[7:4]), .b(4'b0001), .eq(lsl__r));  // open: gt, lt
  Comparator #(.Bits(4)) lsr_r (.a(IW[7:4]), .b(4'b0011), .eq(lsr__r));  // open: gt, lt
  Comparator #(.Bits(3)) lsl_i (.a(IW[6:4]), .b(3'b000), .eq(lsl__i));  // open: gt, lt
  Comparator #(.Bits(3)) lsr_i (.a(IW[6:4]), .b(3'b010), .eq(lsr__i));  // open: gt, lt
  Comparator #(.Bits(8)) mul (.a(IW[27:20]), .b({8{1'b0}}), .eq(mul_eq));  // open: gt, lt
  Comparator #(.Bits(4)) comparator_2 (.a(IW[7:4]), .b(4'b1001), .eq(comparator_2_eq));  // open: gt, lt
  and and_1 (and_1_out, mul_eq, comparator_2_eq);
  Comparator #(.Bits(24)) bx (.a(IW[27:4]), .b(24'h12fff1), .eq(bx_eq));  // open: gt, lt
  Comparator #(.Bits(4)) bl (.a(IW[27:24]), .b(4'b1011), .eq(bl_eq));  // open: gt, lt
  Comparator #(.Bits(4)) b (.a(IW[27:24]), .b(4'b1010), .eq(b_eq));  // open: gt, lt
  Comparator #(.Bits(3)) str_i (.a(IW[27:25]), .b(3'b010), .eq(str_i_eq));  // open: gt, lt
  Comparator #(.Bits(3)) str_r (.a(IW[27:25]), .b(3'b011), .eq(str_r_eq));  // open: gt, lt
  Comparator #(.Bits(3)) ldr_i (.a(IW[27:25]), .b(3'b010), .eq(ldr_i_eq));  // open: gt, lt
  Comparator #(.Bits(3)) ldr_r (.a(IW[27:25]), .b(3'b011), .eq(ldr_r_eq));  // open: gt, lt
  Comparator #(.Bits(8)) mov_i (.a(IW[27:20]), .b(8'h3a), .eq(mov_i_eq));  // open: gt, lt
  Comparator #(.Bits(8)) mov_r (.a(IW[27:20]), .b(8'h1a), .eq(mov_r_eq));  // open: gt, lt
  Comparator #(.Bits(8)) cmp_i (.a(IW[27:20]), .b(8'h35), .eq(cmp_i_eq));  // open: gt, lt
  Comparator #(.Bits(8)) cmp_r (.a(IW[27:20]), .b(8'h15), .eq(cmp_r_eq));  // open: gt, lt
  Comparator #(.Bits(8)) sub_i (.a(IW[27:20]), .b(8'h24), .eq(sub_i_eq));  // open: gt, lt
  Comparator #(.Bits(8)) sub_r (.a(IW[27:20]), .b(8'h4), .eq(sub_r_eq));  // open: gt, lt
  Comparator #(.Bits(8)) add_i (.a(IW[27:20]), .b(8'h28), .eq(add_i_eq));  // open: gt, lt
  Comparator #(.Bits(8)) add_r (.a(IW[27:20]), .b(8'h8), .eq(add_r_eq));  // open: gt, lt
  and and_2 (and_2_out, str_i_eq, ~IW[20]);  // And
  and and_3 (and_3_out, str_r_eq, ~IW[20]);  // And
  and and_4 (and_4_out, ldr_i_eq, IW[20]);
  and and_5 (and_5_out, ldr_r_eq, IW[20]);
  and and_6 (and_6_out, comparator_1_eq, lsl__r);
  and and_7 (and_7_out, comparator_1_eq, lsl__i);
  and and_8 (and_8_out, comparator_1_eq, lsr__r);
  and and_9 (and_9_out, comparator_1_eq, lsr__i);
  PriorityEncoder #(.Selector_Bits(5)) priorityencoder_1 (
    .in0(bx_eq), .in1(bl_eq), .in2(b_eq), .in3(and_2_out), .in4(and_3_out), .in5(and_4_out), .in6(and_5_out),
    .in7(and_6_out), .in8(and_7_out), .in9(and_8_out), .in10(and_9_out), .in11(mov_i_eq), .in12(mov_r_eq),
    .in13(cmp_i_eq), .in14(cmp_r_eq), .in15(sub_i_eq), .in16(sub_r_eq), .in17(add_i_eq), .in18(add_r_eq),
    .in19(and_1_out), .in20(1'b0), .in21(1'b0), .in22(1'b0), .in23(1'b0), .in24(1'b0), .in25(1'b0),
    .in26(1'b0), .in27(1'b0), .in28(1'b0), .in29(1'b0), .in30(1'b0), .in31(1'b0), .num(priorityencoder_1_num));  // open: any
  // Probe on priorityencoder_1_num
  Multiplexer #(.Selector_Bits(5), .Bits(16)) multiplexer_1 (
    .sel(priorityencoder_1_num), .in_0(16'h100), .in_1(16'hd0ac), .in_2(16'h50a0), .in_3(16'h3000),
    .in_4(16'h2000), .in_5(16'hb000), .in_6(16'ha000), .in_7(16'hfa00), .in_8(16'hea00), .in_9(16'hf800),
    .in_10(16'he800), .in_11(16'h9600), .in_12(16'h8600), .in_13(16'h1200), .in_14(16'h200),
    .in_15(16'h9200), .in_16(16'h8200), .in_17(16'h9000), .in_18(16'h8000), .in_19(16'h8410),
    .in_20({16{1'b0}}), .in_21({16{1'b0}}), .in_22({16{1'b0}}), .in_23({16{1'b0}}), .in_24({16{1'b0}}),
    .in_25({16{1'b0}}), .in_26({16{1'b0}}), .in_27({16{1'b0}}), .in_28({16{1'b0}}), .in_29({16{1'b0}}),
    .in_30({16{1'b0}}), .in_31({16{1'b0}}),
    .out({RFW, EXTop, ALUsrcB, ALUop, PCsel, multiplexer_1_out[6], RR0sel, RR1sel, WRsel, WDsel, multiplexer_1_out[1:0]}));
  // Probe on {RFW, EXTop, ALUsrcB, ALUop, PCsel, multiplexer_1_out[6], RR0sel, RR1sel, WRsel, WDsel, multiplexer_1_out[1:0]}
  or or_1 (MR, and_5_out, and_4_out);
  or or_2 (MW, and_3_out, and_2_out);
  or or_3 (CMP, cmp_i_eq, cmp_r_eq);
  // Probe on RFW
  // Probe on EXTop
  // Probe on ALUsrcB
  // Probe on ALUop
  // Probe on PCsel
  // Probe on RR0sel
  // Probe on RR1sel
  // Probe on WRsel
  // Probe on WDsel

  // Other names for the same wires on the sheet: bits6_4[2:0] = IW[6:4]; bits7_4[3:0] = IW[7:4];
  //   bits27_4[23:0] = IW[27:4]; bits27_16[11:0] = IW[27:16]; bit20 = IW[20]; bits27_20[7:0] = IW[27:20];
  //   bits27_24[3:0] = IW[27:24]; bits25_27[2:0] = IW[27:25]; bits28_31[3:0] = IW[31:28]
endmodule
