// Digital circuit reg_input_decoder.dig as structural Verilog
module reg_input_decoder (
  input  mul,
  input  [31:0] iw,
  output [3:0] readreg0,
  output [3:0] writereg,
  output [3:0] readreg1
);

  Multiplexer #(.Bits(4)) multiplexer_1 (.sel(mul), .in_0(iw[19:16]), .in_1(iw[3:0]), .out(readreg0));
  Multiplexer #(.Bits(4)) multiplexer_2 (.sel(mul), .in_0(iw[15:12]), .in_1(iw[19:16]), .out(writereg));
  Multiplexer #(.Bits(4)) multiplexer_3 (.sel(mul), .in_0(iw[3:0]), .in_1(iw[11:8]), .out(readreg1));
endmodule
