// Digital circuit register-file.dig as structural Verilog
module register_file (
  input  [3:0] ReadReg0,
  input  [3:0] ReadReg1,
  input  [31:0] WriteData,
  input  [3:0] WriteReg,
  input  WriteEnable,
  input  CLR,
  input  CLK,
  input  [31:0] PC,
  output [31:0] Rd0,
  output [31:0] Rd1,
  output [31:0] r0,
  output [31:0] r1,
  output [31:0] r2,
  output [31:0] r3,
  output [31:0] r4,
  output [31:0] r5,
  output [31:0] r6,
  output [31:0] r7,
  output [31:0] r8,
  output [31:0] r9,
  output [31:0] r10,
  output [31:0] r11,
  output [31:0] r12,
  output [31:0] r13,
  output [31:0] r14,
  output [31:0] r15
);

  wire decoder_1_r0, decoder_1_r1, decoder_1_r2, decoder_1_r3, decoder_1_r4, decoder_1_r5, decoder_1_r6,
       decoder_1_r7, decoder_1_r8, decoder_1_r9, decoder_1_r10, decoder_1_r11, decoder_1_r12, decoder_1_r13,
       decoder_1_r14;

  decoder decoder_1 (
    .EN(WriteEnable), .SEL(WriteReg), .r0(decoder_1_r0), .r1(decoder_1_r1), .r2(decoder_1_r2),
    .r3(decoder_1_r3), .r4(decoder_1_r4), .r5(decoder_1_r5), .r6(decoder_1_r6), .r7(decoder_1_r7),
    .r8(decoder_1_r8), .r9(decoder_1_r9), .r10(decoder_1_r10), .r11(decoder_1_r11), .r12(decoder_1_r12),
    .r13(decoder_1_r13), .r14(decoder_1_r14));  // open: r15
  _32bit_register u_r0 (.Data(WriteData), .EN(decoder_1_r0), .CLR(CLR), .CLK(CLK), .Q(r0));
  _32bit_register u_r1 (.Data(WriteData), .EN(decoder_1_r1), .CLR(CLR), .CLK(CLK), .Q(r1));
  _32bit_register u_r2 (.Data(WriteData), .EN(decoder_1_r2), .CLR(CLR), .CLK(CLK), .Q(r2));
  _32bit_register u_r3 (.Data(WriteData), .EN(decoder_1_r3), .CLR(CLR), .CLK(CLK), .Q(r3));
  _32bit_register u_r4 (.Data(WriteData), .EN(decoder_1_r4), .CLR(CLR), .CLK(CLK), .Q(r4));
  _32bit_register u_r5 (.Data(WriteData), .EN(decoder_1_r5), .CLR(CLR), .CLK(CLK), .Q(r5));
  _32bit_register u_r6 (.Data(WriteData), .EN(decoder_1_r6), .CLR(CLR), .CLK(CLK), .Q(r6));
  _32bit_register u_r7 (.Data(WriteData), .EN(decoder_1_r7), .CLR(CLR), .CLK(CLK), .Q(r7));
  _32bit_register u_r8 (.Data(WriteData), .EN(decoder_1_r8), .CLR(CLR), .CLK(CLK), .Q(r8));
  _32bit_register u_r9 (.Data(WriteData), .EN(decoder_1_r9), .CLR(CLR), .CLK(CLK), .Q(r9));
  _32bit_register u_r10 (.Data(WriteData), .EN(decoder_1_r10), .CLR(CLR), .CLK(CLK), .Q(r10));
  _32bit_register u_r11 (.Data(WriteData), .EN(decoder_1_r11), .CLR(CLR), .CLK(CLK), .Q(r11));
  _32bit_register u_r12 (.Data(WriteData), .EN(decoder_1_r12), .CLR(CLR), .CLK(CLK), .Q(r12));
  _32bit_register u_r13 (.Data(WriteData), .EN(decoder_1_r13), .CLR(CLR), .CLK(CLK), .Q(r13));
  _32bit_register u_r14 (.Data(WriteData), .EN(decoder_1_r14), .CLR(CLR), .CLK(CLK), .Q(r14));
  Multiplexer #(.Selector_Bits(4), .Bits(32)) multiplexer_1 (
    .sel(ReadReg0), .in_0(r0), .in_1(r1), .in_2(r2), .in_3(r3), .in_4(r4), .in_5(r5), .in_6(r6), .in_7(r7),
    .in_8(r8), .in_9(r9), .in_10(r10), .in_11(r11), .in_12(r12), .in_13(r13), .in_14(r14), .in_15(PC),
    .out(Rd0));
  Multiplexer #(.Selector_Bits(4), .Bits(32)) multiplexer_2 (
    .sel(ReadReg1), .in_0(r0), .in_1(r1), .in_2(r2), .in_3(r3), .in_4(r4), .in_5(r5), .in_6(r6), .in_7(r7),
    .in_8(r8), .in_9(r9), .in_10(r10), .in_11(r11), .in_12(r12), .in_13(r13), .in_14(r14), .in_15(PC),
    .out(Rd1));

  assign r15 = PC;
endmodule
